# Fritzing sketch slave_pcb (saved by Fritzing 0.9.3b)
circuit board: 7.79362cm x 7.73231cm
breadboards: 1

parts:
  2N7000-WW = MOSFET-NCHANNEL [package=to-92]
  2n7000-W = MOSFET-NCHANNEL [package=to-92]
  Feather_M4_Express = Adafruit Feather M0 Basic Proto [part_number="Adafruit #2772"]
  Airlift_Breakout = Brian's AirLift ESP32 Coprocessor
  4_7k = Resistor [tolerance=±5% resistance=4.7k package=THT]
  4_7k_2 = Resistor [tolerance=±5% resistance=4.7k package=THT]
  G_IRT = female pin header, 2 pins [form="♀ (female)"]
  SDA_SCL = female pin header, 2 pins [form="♀ (female)"]
  G_IRR = female pin header, 2 pins [form="♀ (female)"]
  12v_G_5v = female pin header, 3 pins [form="♀ (female)"]
  W_12v_WW = female pin header, 3 pins [form="♀ (female)"]
  G_Neo_5v = female pin header, 3 pins [form="♀ (female)"]

nets:
  N1: 2N7000-WW.D, W_12v_WW.pin1
  GND: 2N7000-WW.S, 2n7000-W.S, Airlift_Breakout.GND#22, G_IRT.pin2, G_IRR.pin2, 12v_G_5v.pin2, G_Neo_5v.pin3
  N2: 2N7000-WW.G, Feather_M4_Express.D12
  N3: 2n7000-W.D, W_12v_WW.pin3
  N4: 2n7000-W.G, Feather_M4_Express.D11
  N5: Feather_M4_Express.D1, G_IRR.pin1
  N6: Feather_M4_Express.D0, G_IRT.pin1
  N7: Feather_M4_Express.MISO, Airlift_Breakout.MISO
  N8: Feather_M4_Express.MOSI, Airlift_Breakout.MOSI
  N9: Feather_M4_Express.SCK, Airlift_Breakout.SCK
  5V: Feather_M4_Express.VBUS, Airlift_Breakout.VIN#24, Airlift_Breakout.GND#27, 4_7k.Pin_0, 4_7k_2.Pin_0, 12v_G_5v.pin1, G_Neo_5v.pin1
  N10: Feather_M4_Express.D13, G_Neo_5v.pin2
  N11: Feather_M4_Express.D10, Airlift_Breakout.CS
  N12: Feather_M4_Express.D9, Airlift_Breakout.BUSY
  N13: Feather_M4_Express.D6, Airlift_Breakout.RST
  N14: Feather_M4_Express.SCL, 4_7k.Pin_1, SDA_SCL.pin1
  N15: Feather_M4_Express.SDA, 4_7k_2.Pin_1, SDA_SCL.pin2
  12V: 12v_G_5v.pin3, W_12v_WW.pin2

notes:
  Mapping of mpr121 to airlift breakout board
  TX0 ELEC10
  RXI ELEC9
  GPO ELEC8
  RST ELEC7
  BUSY ELEC6
  CS ELEC5
  MOSI ELEC4
  MISO ELEC3
  SCK ELEC2
  GND ELEC1
  3Vo ELEC0
  VIN GND

custom parts:
  Adafruit Feather M0 Basic Proto: At the Feather M0's heart is an ATSAMD21G18 ARM Cortex M0 processor, clocked at 48 MHz and at 3.3V logic, the same one used in the new Arduino Zero. This chip has a whopping 256K of FLASH (8x more than the Atmega328 or 32u4) and 32K of RAM (16x as much)! This chip comes with built in USB so it has USB-to-Serial program & debug capability built in with no need for an FTDI-like chip. To make it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
  Brian's AirLift ESP32 Coprocessor: Add lots of touch sensors to your next microcontroller project with this easy-to-use 12-channel capacitive touch sensor breakout board, starring the MPR121. This chip can handle up to 12 individual touch pads. The MPR121 has support for only I2C, which can be implemented with nearly any microcontroller. You can select one of 4 addresses with the ADDR pin, for a total of 48 capacitive touch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
