# Fritzing sketch slave_pcb2 (saved by Fritzing 0.9.3b)
circuit board: 7.79362cm x 7.42033cm
breadboards: 1

parts:
  WW_Fet = MOSFET-NCHANNEL [package=to-92]
  W_Fet = MOSFET-NCHANNEL [package=to-92]
  IR_Trans = Camdenboss CTB0158-2 [part_number=CTB0158-2 package=THT]
  W_LED_WW = Camdenboss CTB0158-3 [part_number=CTB0158-3 package=THT]
  Feather_M4_Express = Adafruit Feather M0 Basic Proto [part_number="Adafruit #2772"]
  Airlift_Breakout = Brian's AirLift ESP32 Coprocessor
  IR_Receiv = Camdenboss CTB0158-2 [part_number=CTB0158-2 package=THT]
  12v_G_5v = Camdenboss CTB0158-3 [part_number=CTB0158-3 package=THT]
  Neopixel = Camdenboss CTB0158-3 [part_number=CTB0158-3 package=THT]
  I2C = Camdenboss CTB0158-4 [part_number=CTB0158-4 package=THT]
  R1 = Resistor [tolerance=±10% resistance=4.7k package="0805 [SMD]"]  # not connected

nets (from the pcb view):
  N1: WW_Fet.D, W_LED_WW.pin1
  N2: WW_Fet.S, W_Fet.S, IR_Trans.pin2, Airlift_Breakout.GND#22, IR_Receiv.pin2, 12v_G_5v.pin2, Neopixel.pin3
  N3: WW_Fet.G, Feather_M4_Express.D12
  N4: W_Fet.D, W_LED_WW.pin3
  N5: W_Fet.G, Feather_M4_Express.D11
  N6: IR_Trans.pin1, Feather_M4_Express.D0
  N7: W_LED_WW.pin2, 12v_G_5v.pin3
  N8: Feather_M4_Express.D1, IR_Receiv.pin1
  N9: Feather_M4_Express.MISO, Airlift_Breakout.MISO
  N10: Feather_M4_Express.MOSI, Airlift_Breakout.MOSI
  N11: Feather_M4_Express.SCK, Airlift_Breakout.SCK
  N12: Feather_M4_Express.A5, I2C.pin4
  N13: Feather_M4_Express.VBUS, Airlift_Breakout.VIN#24, Airlift_Breakout.GND#27, 12v_G_5v.pin1, Neopixel.pin1
  N14: Feather_M4_Express.D13, Neopixel.pin2
  N15: Feather_M4_Express.D10, Airlift_Breakout.CS
  N16: Feather_M4_Express.D9, Airlift_Breakout.BUSY
  N17: Feather_M4_Express.D6, Airlift_Breakout.RST
  N18: Feather_M4_Express.D5, I2C.pin1
  N19: Feather_M4_Express.SCL, I2C.pin2
  N20: Feather_M4_Express.SDA, I2C.pin3

notes:
  Mapping of mpr121 to airlift breakout board
  TX0 ELEC10
  RXI ELEC9
  GPO ELEC8
  RST ELEC7
  BUSY ELEC6
  CS ELEC5
  MOSI ELEC4
  MISO ELEC3
  SCK ELEC2
  GND ELEC1
  3Vo ELEC0
  VIN GND

custom parts:
  Adafruit Feather M0 Basic Proto: At the Feather M0's heart is an ATSAMD21G18 ARM Cortex M0 processor, clocked at 48 MHz and at 3.3V logic, the same one used in the new Arduino Zero. This chip has a whopping 256K of FLASH (8x more than the Atmega328 or 32u4) and 32K of RAM (16x as much)! This chip comes with built in USB so it has USB-to-Serial program & debug capability built in with no need for an FTDI-like chip. To make it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
  Brian's AirLift ESP32 Coprocessor: Add lots of touch sensors to your next microcontroller project with this easy-to-use 12-channel capacitive touch sensor breakout board, starring the MPR121. This chip can handle up to 12 individual touch pads. The MPR121 has support for only I2C, which can be implemented with nearly any microcontroller. You can select one of 4 addresses with the ADDR pin, for a total of 48 capacitive touch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
