# Fritzing sketch slave_pcb3 (saved by Fritzing 0.9.3b)
circuit board: 8.2cm x 7.7cm
breadboards: 1

parts:
  WW_Fet = MOSFET-NCHANNEL [package=to-92]
  W_Fet = MOSFET-NCHANNEL [package=to-92]
  Feather_M4_Express = Adafruit Feather M4 Express [part_number="Adafruit #3857"]
  R1 = Resistor [tolerance=±5% resistance=4.7k package=THT]
  R2 = Resistor [tolerance=±5% resistance=4.7k package=THT]
  Airlift_Breakout = Adafruit AirLift Breakout [part_number="Adafruit #4201"]
  +_12v_- = Baxboss CTB0158-2 [part_number=CTB0158-2 package=THT]
  12v_G_5v = Baxboss CTB0158-3 [part_number=CTB0158-3 package=THT]
  W_LED_WW = Baxboss CTB0158-3 [part_number=CTB0158-3 package=THT]
  Neo_Gnd_D_5v = Baxboss CTB0158-3 [part_number=CTB0158-3 package=THT]
  SCL_SDA = Baxboss CTB0158-2 [part_number=CTB0158-2 package=THT]
  IR_Rec = Baxboss CTB0158-2 [part_number=CTB0158-2 package=THT]
  IR_Trans = Baxboss CTB0158-2 [part_number=CTB0158-2 package=THT]

nets:
  N1: WW_Fet.D, W_LED_WW.pin1
  GND: WW_Fet.S, W_Fet.S, Airlift_Breakout.GND, +_12v_-.pin2, 12v_G_5v.pin2, Neo_Gnd_D_5v.pin3, IR_Rec.pin2, IR_Trans.pin2
  N2: WW_Fet.G, Feather_M4_Express.D12
  N3: W_Fet.D, W_LED_WW.pin3
  N4: W_Fet.G, Feather_M4_Express.D11
  N5: Feather_M4_Express.TX_D1, IR_Rec.pin1
  N6: Feather_M4_Express.RX_D0, IR_Trans.pin1
  N7: Feather_M4_Express.MISO, Airlift_Breakout.MISO
  N8: Feather_M4_Express.MOSI, Airlift_Breakout.MOSI
  N9: Feather_M4_Express.SCK, Airlift_Breakout.SCK
  5V: Feather_M4_Express.VBUS, Airlift_Breakout.VIN, 12v_G_5v.pin1
  N10: Feather_M4_Express.D13, Neo_Gnd_D_5v.pin2
  N11: Feather_M4_Express.D10, Airlift_Breakout.CS
  N12: Feather_M4_Express.D9, Airlift_Breakout.ESP_BUSY
  N13: Feather_M4_Express.D6, Airlift_Breakout.RESET
  N14: Feather_M4_Express.SCL, R1.Pin_0, SCL_SDA.pin1
  N15: Feather_M4_Express.SDA, R2.Pin_0, SCL_SDA.pin2
  N16: R1.Pin_1, R2.Pin_1, Neo_Gnd_D_5v.pin1
  12V: +_12v_-.pin1, 12v_G_5v.pin3, W_LED_WW.pin2

notes:
  Mapping of mpr121 to airlift breakout board
  TX0 ELEC10
  RXI ELEC9
  GPO ELEC8
  RST ELEC7
  BUSY ELEC6
  CS ELEC5
  MOSI ELEC4
  MISO ELEC3
  SCK ELEC2
  GND ELEC1
  3Vo ELEC0
  VIN GND

custom parts:
  Adafruit Feather M4 Express: It's what you've been waiting for, the Feather M4 Express featuring ATSAMD51. This Feather is fast like a swift, smart like an owl, strong like a ox-bird (it's half ox, half bird, OK?) This feather is powered by our new favorite chip, the ATSAMD51J19 - with its 120MHz Cortex M4 with floating point support and 512KB Flash and 192KB RAM. Your code will zig and zag and zoom, and with a bunch of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
  Adafruit AirLift Breakout: Give your plain ol' microcontroller project a lift with the Adafruit AirLift - a breakout board that lets you use the powerful ESP32 as a WiFi co-processor. You probably have your favorite microcontroller (like the ATmega328 or ATSAMD51), awesome peripherals and lots of libraries. But it doesn't have WiFi built in! So lets give that chip a best friend, the ESP32. This chip can handle all the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
  Baxboss CTB0158-2: Camdenboss CTB0158-2 5.08mm (0.2") Pitch Standard Profile 90 ̊ Rising Clamp Terminal, 2 pole The real-life connectors are modular, made up of two or three connector blocks slotted together. These can be further slotted together to make larger connectors. Fritzing part is derived from Screw terminals by Lionel Michel. Because of the offset between connection pins and screw terminals, these are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
  Baxboss CTB0158-3: Camdenboss CTB0158-3 5.08mm (0.2") Pitch Standard Profile 90 ̊ Rising Clamp Terminal, 3 pole The real-life connectors are modular, made up of two or three connector blocks slotted together. These can be further slotted together to make larger connectors. Fritzing part is derived from Screw terminals by Lionel Michel. Because of the offset between connection pins and screw terminals, these are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
