# Fritzing sketch slave_pcb6 (saved by Fritzing 0.9.3b)
circuit board: 11cm x 7.7cm
breadboards: 1

parts:
  Feather_M4_Express = Adafruit Feather M4 Express [part_number="Adafruit #3857"]
  R1 = Resistor [tolerance=±5% resistance=4.7k package=THT]
  R2 = Resistor [tolerance=±5% resistance=4.7k package=THT]
  Airlift_Breakout = Adafruit AirLift Breakout [part_number="Adafruit #4201"]
  +_12v_- = Baxboss CTB0158-2 [part_number=CTB0158-2 package=THT]
  5v_G_12v = Baxboss CTB0158-3 [part_number=CTB0158-3 package=THT]
  WW_LED_W = Baxboss CTB0158-3 [part_number=CTB0158-3 package=THT]
  Neo_Gnd_D_5v = Baxboss CTB0158-3 [part_number=CTB0158-3 package=THT]
  SCL_SDA = Baxboss CTB0158-2 [part_number=CTB0158-2 package=THT]
  IR_Trans = Baxboss CTB0158-2 [part_number=CTB0158-2 package=THT]
  IR_Rec = Baxboss CTB0158-2 [part_number=CTB0158-2 package=THT]
  R3 = Resistor [tolerance=±5% resistance=47 package=THT]
  Pgm_Run = SPST Switch [package=switch-spdt]
  RFU_3v3_A2_D2_D3 = Camdenboss CTB0158-4 [part_number=CTB0158-4 package=THT]
  W_Fet = MOSFET-NCHANNEL [package=to-92]
  WW_Fet = MOSFET-NCHANNEL [package=to-92]
  SW1 = DIP Switch 8 Position [package=dipswitch-08]
  R4 = Resistor [tolerance=±5% resistance=100k package=THT]
  R5 = Resistor [tolerance=±5% resistance=47k package=THT]
  R6 = Resistor [tolerance=±5% resistance=22k package=THT]
  R7 = Resistor [tolerance=±5% resistance=10k package=THT]
  R8 = Resistor [tolerance=±5% resistance=4.7k package=THT]
  R9 = Resistor [tolerance=±5% resistance=10k package=THT]

nets:
  N1: Feather_M4_Express.D4, RFU_3v3_A2_D2_D3.pin3
  N2: Feather_M4_Express.TX_D1, R3.Pin_1
  N3: Feather_M4_Express.RX_D0, IR_Rec.pin1
  N4: Feather_M4_Express.MISO, Airlift_Breakout.MISO
  N5: Feather_M4_Express.MOSI, Airlift_Breakout.MOSI
  N6: Feather_M4_Express.SCK, Airlift_Breakout.SCK
  N7: Feather_M4_Express.A5, Pgm_Run.O
  N8: Feather_M4_Express.A2, RFU_3v3_A2_D2_D3.pin2
  N9: Feather_M4_Express.A1, R4.Pin_0, R5.Pin_0, R6.Pin_0, R7.Pin_0, R8.Pin_0, R9.Pin_0
  GND: Feather_M4_Express.GND, Airlift_Breakout.GND, +_12v_-.pin2, 5v_G_12v.pin2, Neo_Gnd_D_5v.pin3, IR_Trans.pin2, IR_Rec.pin2, Pgm_Run.P, W_Fet.S, WW_Fet.S, R9.Pin_1
  N10: Feather_M4_Express.+3V3, RFU_3v3_A2_D2_D3.pin1
  5V: Feather_M4_Express.VBUS, R1.Pin_1, R2.Pin_1, Airlift_Breakout.VIN, 5v_G_12v.pin1, Neo_Gnd_D_5v.pin1, SW1.1, SW1.2, SW1.3, SW1.4, SW1.5
  N11: Feather_M4_Express.D13, Neo_Gnd_D_5v.pin2
  N12: Feather_M4_Express.D12, WW_Fet.G
  N13: Feather_M4_Express.D11, W_Fet.G
  N14: Feather_M4_Express.D10, Airlift_Breakout.CS
  N15: Feather_M4_Express.D9, Airlift_Breakout.ESP_BUSY
  N16: Feather_M4_Express.D6, Airlift_Breakout.RESET
  N17: Feather_M4_Express.D5, RFU_3v3_A2_D2_D3.pin4
  N18: Feather_M4_Express.SCL, R1.Pin_0, SCL_SDA.pin1
  N19: Feather_M4_Express.SDA, R2.Pin_0, SCL_SDA.pin2
  12V: +_12v_-.pin1, 5v_G_12v.pin3, WW_LED_W.pin2
  N20: WW_LED_W.pin1, WW_Fet.D
  N21: WW_LED_W.pin3, W_Fet.D
  N22: IR_Trans.pin1, R3.Pin_0
  N23: SW1.12, R8.Pin_1
  N24: SW1.13, R7.Pin_1
  N25: SW1.14, R6.Pin_1
  N26: SW1.15, R5.Pin_1
  N27: SW1.16, R4.Pin_1

custom parts:
  Adafruit Feather M4 Express: It's what you've been waiting for, the Feather M4 Express featuring ATSAMD51. This Feather is fast like a swift, smart like an owl, strong like a ox-bird (it's half ox, half bird, OK?) This feather is powered by our new favorite chip, the ATSAMD51J19 - with its 120MHz Cortex M4 with floating point support and 512KB Flash and 192KB RAM. Your code will zig and zag and zoom, and with a bunch of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
  Adafruit AirLift Breakout: Give your plain ol' microcontroller project a lift with the Adafruit AirLift - a breakout board that lets you use the powerful ESP32 as a WiFi co-processor. You probably have your favorite microcontroller (like the ATmega328 or ATSAMD51), awesome peripherals and lots of libraries. But it doesn't have WiFi built in! So lets give that chip a best friend, the ESP32. This chip can handle all the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
  Baxboss CTB0158-2: Camdenboss CTB0158-2 5.08mm (0.2") Pitch Standard Profile 90 ̊ Rising Clamp Terminal, 2 pole The real-life connectors are modular, made up of two or three connector blocks slotted together. These can be further slotted together to make larger connectors. Fritzing part is derived from Screw terminals by Lionel Michel. Because of the offset between connection pins and screw terminals, these are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
  Baxboss CTB0158-3: Camdenboss CTB0158-3 5.08mm (0.2") Pitch Standard Profile 90 ̊ Rising Clamp Terminal, 3 pole The real-life connectors are modular, made up of two or three connector blocks slotted together. These can be further slotted together to make larger connectors. Fritzing part is derived from Screw terminals by Lionel Michel. Because of the offset between connection pins and screw terminals, these are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
  MOSFET-NCHANNEL: Generic NMOS footprint
